# Fritzing sketch Schematics (saved by Fritzing 0.9.3b)
circuit board: 8.46667cm x 5.64444cm
breadboards: 1

parts:
  Part1 = Photon
  OLED1 = 128x64 Monochrom OLED Display with SPI Control

nets:
  GND: Part1.GND, OLED1.GND
  VIN: Part1.VIN, OLED1.Vin
  N1: Part1.D0, OLED1.Data
  N2: Part1.D1, OLED1.Clock
  N3: Part1.D2, OLED1.SA0/DC
  N4: Part1.D3, OLED1.CS
  N5: Part1.D4, OLED1.Reset
